# Fritzing sketch pumpkin_wiring (saved by Fritzing 0.9.3b)
breadboards: 1

parts:
  Part1 = Photon
  hc-sr1 = hc-sr04
  J1 = Piezo Speaker
  R2 = Resistor [tolerance=±5% resistance=47 package="0603 [SMD]"]
  R3 = Resistor [tolerance=±5% resistance=10 package="0603 [SMD]"]
  R4 = Resistor [tolerance=±5% resistance=10 package="0603 [SMD]"]
  R5 = Resistor [tolerance=±5% resistance=47 package="0603 [SMD]"]
  R6 = Resistor [tolerance=±5% resistance=10 package="0603 [SMD]"]
  LED1 = LED - 3mm [color="Red (633nm)" package="3 mm [THT]"]
  LED4 = smd LED [color="Green (565nm)" package="0603 [SMD]"]
  LED5 = LED - 3mm [color="Green (560nm)" package="3 mm [THT]"]
  LED6 = LED - 3mm [color="Blue (470nm)" package="3 mm [THT]"]
  LED7 = LED - 3mm [color="Red (633nm)" package="3 mm [THT]"]
  LED8 = LED - 3mm [color="Blue (470nm)" package="3 mm [THT]"]
  LED9 = LED - 3mm [color="Green (560nm)" package="3 mm [THT]"]
  Part2 = Photon
  LED10 = LED - 3mm [color="Red (633nm)" package="3 mm [THT]"]
  LED11 = LED - 3mm [color="Red (633nm)" package="3 mm [THT]"]
  LED12 = smd LED [color="Green (565nm)" package="0603 [SMD]"]
  J2 = Piezo Speaker
  Part3 = Photon

nets:
  N1: Part1.A0, Part2.A0, Part3.A0
  N2: Part1.A1, Part2.A1, Part3.A1
  N3: Part1.A2, Part2.A2, Part3.A2
  N4: Part1.A3, Part2.A3, Part3.A3
  N5: Part1.A4, Part2.A4, Part3.A4
  N6: Part1.A5, J1.pin2, Part2.A5, J2.pin2, Part3.A5
  N7: Part1.DAC, Part2.DAC, Part3.DAC
  N8: Part1.WKP, Part2.WKP, Part3.WKP
  N9: Part1.RX, Part2.RX, Part3.RX
  N10: Part1.TX, Part2.TX, Part3.TX
  GND: Part1.GND, hc-sr1.GND, J1.pin1, LED1.cathode, LED4.cathode, LED5.cathode, LED6.cathode, LED7.cathode, LED8.cathode, LED9.cathode, Part2.GND, LED10.cathode, LED11.cathode, LED12.cathode, J2.pin1, Part3.GND
  VIN: Part1.VIN, hc-sr1.VCC, Part2.VIN, Part3.VIN
  N11: Part1.D0, hc-sr1.Echo, Part2.D0, Part3.D0
  N12: Part1.D1, hc-sr1.Trig, Part2.D1, Part3.D1
  N13: Part1.D2, R6.Pin_0, Part2.D2, Part3.D2
  N14: Part1.D3, R5.Pin_0, Part2.D3, Part3.D3
  N15: Part1.D4, R2.Pin_0, Part2.D4, Part3.D4
  N16: Part1.D5, R4.Pin_0, Part2.D5, Part3.D5
  N17: Part1.D6, R3.Pin_0, Part2.D6, Part3.D6
  N18: Part1.D7, Part2.D7, Part3.D7
  N19: Part1.VBAT, Part2.VBAT, Part3.VBAT
  N20: Part1.RST, Part2.RST, Part3.RST
  3V3: Part1.3V3, Part2.3V3, Part3.3V3
  N21: R2.Pin_1, LED1.anode, LED7.anode
  N22: R3.Pin_1, LED6.anode, LED8.anode
  N23: R4.Pin_1, LED5.anode, LED9.anode
  N24: R5.Pin_1, LED10.anode, LED11.anode
  N25: R6.Pin_1, LED4.anode, LED12.anode

notes:
  Make sure to use a quality 5V power supply, voltage irregularities can cause the range finder to misread the distance.
  animated LEDs for song
  (ideal resistors may vary)
  background
  LEDs
